# Fritzing sketch ESP8266WiFi_DS18B20 (saved by Fritzing 0.9.4)
circuit board: 8.46667cm x 5.64444cm

parts:
  U1 = ESP8266 NodeMCU LoLin module
  Power_plug1 = Power plug
  REG1 = LD33 Low-Dropout Voltage Regulator
  LED1 = LED - 5mm [color="Red (633nm)" package="5 mm [THT]"]
  R1 = Resistor [tolerance=±5% resistance=680 package=THT]
  S1 = Taiway 100-SP-X-T1 SPDT Miniature Toggle Switch [part_number=100-SP-X-T1-0-0-B1-M1 package=THT]
  D1 = Rectifier Diode [part_number=1N4001 package="300 mil [THT]"]
  C1 = Electrolytic Capacitor [capacitance=10µF package="100 mil [THT, electrolytic]"]
  C2 = Electrolytic Capacitor [capacitance=100µF package="100 mil [THT, electrolytic]"]
  DS1 = DS18B20 1-Wire Temperature Sensor [part_number=DS18B20]
  DS2 = DS18B20 1-Wire Temperature Sensor [part_number=DS18B20]

nets:
  N1: U1.D1, DS1.DQ
  N2: U1.D2, DS2.DQ
  VDD: U1.3V3, REG1.Vout, C2.+, DS1.VDD, DS2.VDD
  GND: U1.GND, Power_plug1.GND, REG1.GND, LED1.cathode, C1.-, C2.-, DS1.GND, DS2.GND
  N3: Power_plug1.VCC, D1.anode
  N4: REG1.Vin, R1.Pin_1, S1.L1, C1.+
  N5: LED1.anode, R1.Pin_0
  N6: S1.COM, D1.cathode

notes:
  Sensor_1
  Sensor_2
  680R
  DC +7,5V
  1N4001
  SWITCH
  10uF
  100uF

custom parts:
  ESP8266 NodeMCU LoLin module: ESP8266 based NodeMCU

// code stored in the sketch: ESP8266_DHT22.ino

